// Digital circuit mini_cpu.dig as structural Verilog
module mini_cpu (
  input  [7:0] M,
  input  [7:0] N,
  input  clk,
  input  [12:0] progIN,
  input  progLoad,
  input  result,
  input  reset,
  input  start,
  output [7:0] \output ,
  output valid,
  output done
);

  wire and_2_out, and_3_out, and_4_out, and_6_out, and_9_out, and_11_out, and_12_out, and_13_out, and_14_out,
       and_15_out, and_16_out, and_17_out, and_18_out, as, bs, comparator_1_eq, comparator_4_eq,
       comparator_5_eq, comparator_5_gt, comparator_5_lt, cs, delay_3_out, eFlag, gFlag, jump, lFlag,
       multiplexer_14_out, or_1_out, or_2_out, or_3_out, or_4_out, or_6_out, or_7_out, or_8_out, or_11_out,
       or_12_out, or_13_out, or_14_out, or_15_out, prime_d, re, readRam, rehold, resetstop, restop,
       resulthold, sigB, sigComp, sigJump, sigJump_eq, sigJump_eq__gt, sigJump_gt, sigJump_lt, sigPrime,
       sigRam, st, starthold;
  wire [1:0] c_store_d, d_ff_10_q;
  wire [2:0] abc_store_d;
  wire [3:0] a_store_d, d_ff_9_q;
  wire [4:0] d_ff_3_q, d_ff_7_q, delay_2_out, delay_4_out, multiplexer_7_out, opcode;
  wire [7:0] A, add_1_s, add_2_s, and_10_out, B, barrelshifter_1_out, C, counter_1_out, counter_2_out,
       d_ff_2_q, d_ff_6_q, delay_1_out, div_1_q, div_1_r, mul_1_mul, multiplexer_1_out, multiplexer_2_out,
       multiplexer_3_out, multiplexer_4_out, multiplexer_5_out, multiplexer_10_out, multiplexer_12_out,
       multiplexer_13_out, multiplexer_15_out, multiplexer_16_out, multiplexer_19_out, Noperand, not_1_out,
       operand, or_9_out, rA, ramdualaccess_1_d2, rom_1_d, sub_1_s, xor_1_out;
  wire [9:0] rom_2_d;
  wire [12:0] multiplexer_6_out, ramdualaccess_2_d1, ramdualaccess_2_d2;

  Multiplexer #(.Bits(8)) multiplexer_1 (.sel(or_1_out), .in_0({8{1'b0}}), .in_1(add_1_s), .out(multiplexer_1_out));
  or or_1 (or_1_out, progLoad, starthold);
  Counter #(.Bits(8)) counter_1 (.en(rehold), .C(clk), .clr(~rehold), .out(counter_1_out));  // open: ovf
  D_FF d_ff_1 (.D(start), .C(clk), .Q(st));  // open: nQ
  Comparator #(.Bits(5)) comparator_1 (.a(opcode), .b({5{1'b1}}), .eq(comparator_1_eq));  // open: gt, lt
  Comparator #(.Bits(8)) comparator_2 (.a(counter_1_out), .b(8'h10), .eq(resetstop));  // open: gt, lt
  Multiplexer #(.Bits(8)) multiplexer_2 (.sel(rehold), .in_0(A), .in_1({8{1'b0}}), .out(multiplexer_2_out));
  and and_1 (starthold, ~start, or_2_out);  // And
  or or_2 (or_2_out, start, and_2_out);
  and and_2 (and_2_out, ~re, ~comparator_1_eq, or_2_out);  // And
  Add #(.Bits(8)) add_1 (.a(d_ff_2_q), .b(8'h1), .c_i(1'b0), .s(add_1_s));  // open: c_o
  Multiplexer #(.Bits(8)) multiplexer_3 (.sel(jump), .in_0(multiplexer_1_out), .in_1(operand), .out(multiplexer_3_out));
  Multiplexer #(.Bits(8)) multiplexer_4 (.sel(rehold), .in_0(operand), .in_1(counter_1_out), .out(multiplexer_4_out));
  D_FF #(.Bits(8)) d_ff_2 (.D(multiplexer_3_out), .C(clk), .Q(d_ff_2_q));  // open: nQ
  or or_3 (or_3_out, rehold, sigRam);
  Counter #(.Bits(8)) counter_2 (.en(resulthold), .C(clk), .clr(~resulthold), .out(counter_2_out));  // open: ovf
  or or_4 (or_4_out, resulthold, readRam);
  or or_5 (resulthold, result, and_4_out);
  RAMDualAccess #(.AddrBits(8), .Bits(8)) ramdualaccess_1 (
    .str(or_3_out), .C(clk), .ld(or_4_out), .A1(multiplexer_4_out), .Din1(multiplexer_2_out),
    .A2(counter_2_out), .D1(rA), .D2(ramdualaccess_1_d2));
  or or_6 (or_6_out, and_3_out, st);
  and and_3 (and_3_out, or_6_out, ~re);  // And
  and and_4 (and_4_out, ~restop, resulthold);  // And
  Comparator #(.Bits(8)) comparator_3 (.a(counter_2_out), .b(8'h11), .eq(restop));  // open: gt, lt
  and and_5 (valid, or_6_out, ~st);  // And
  RAMDualAccess #(.AddrBits(8), .Bits(13)) ramdualaccess_2 (
    .str(progLoad), .C(clk), .ld(starthold), .A1(d_ff_2_q), .Din1(progIN), .A2(operand),
    .D1(ramdualaccess_2_d1), .D2(ramdualaccess_2_d2));
  D_FF #(.Bits(5)) d_ff_3 (.D(opcode), .C(clk), .Q(d_ff_3_q));  // open: nQ
  Multiplexer #(.Bits(8)) multiplexer_5 (
    .sel(resulthold), .in_0({8{1'b0}}), .in_1(ramdualaccess_1_d2), .out(multiplexer_5_out));
  Multiplexer #(.Bits(13)) multiplexer_6 (
    .sel(starthold), .in_0({13{1'b0}}), .in_1(ramdualaccess_2_d1), .out(multiplexer_6_out));
  Delay #(.Bits(8)) delay_1 (.in(multiplexer_5_out), .out(delay_1_out));
  Delay #(.Bits(5), .delayTime(2)) delay_2 (.in(multiplexer_6_out[12:8]), .out(delay_2_out));
  Comparator #(.Bits(5)) comparator_4 (.a(d_ff_3_q), .b(5'b01001), .eq(comparator_4_eq));  // open: gt, lt
  D_FF #(.Bits(8)) d_ff_4 (.D(delay_1_out), .C(and_6_out), .Q(\output ));  // open: nQ
  and and_6 (and_6_out, clk, resulthold);
  and and_7 (done, ~re, ~result, ~st, or_7_out, ~progLoad);  // And
  Delay delay_3 (.in(reset), .out(delay_3_out));
  Multiplexer #(.Bits(5)) multiplexer_7 (.sel(jump), .in_0(delay_2_out), .in_1({5{1'b0}}), .out(multiplexer_7_out));
  Multiplexer #(.Bits(8)) multiplexer_8 (
    .sel(comparator_4_eq), .in_0({8{1'b0}}), .in_1(ramdualaccess_2_d2[7:0]), .out(Noperand));
  or or_7 (or_7_out, restop, done);
  and and_8 (rehold, ~resetstop, or_8_out);  // And
  or or_8 (or_8_out, re, and_9_out);
  D_FF d_ff_5 (.D(delay_3_out), .C(clk), .Q(re));  // open: nQ
  D_FF #(.Bits(8)) d_ff_6 (.D(multiplexer_6_out[7:0]), .C(clk), .Q(d_ff_6_q));  // open: nQ
  D_FF #(.Bits(5)) d_ff_7 (.D(multiplexer_7_out), .C(clk), .Q(d_ff_7_q));  // open: nQ
  and and_9 (and_9_out, ~resetstop, rehold);  // And
  Delay #(.Bits(5), .delayTime(2)) delay_4 (.in(d_ff_7_q), .out(delay_4_out));
  D_FF #(.Bits(8)) d_ff_8 (.D(d_ff_6_q), .C(clk), .Q(operand));  // open: nQ
  Multiplexer #(.Bits(5)) multiplexer_9 (.sel(jump), .in_0(delay_4_out), .in_1({5{1'b0}}), .out(opcode));
  Seven_Seg_Hex seven_seg_hex_1 (.d(\output [7:4]), .dp(1'b0));
  Seven_Seg_Hex seven_seg_hex_2 (.d(\output [3:0]), .dp(1'b0));
  Add #(.Bits(8)) add_2 (.a(A), .b(B), .c_i(1'b0), .s(add_2_s));  // open: c_o
  Sub #(.Bits(8)) sub_1 (.a(A), .b(B), .c_i(1'b0), .s(sub_1_s));  // open: c_o
  Mul #(.Bits(4)) mul_1 (.a(A[3:0]), .b(B[3:0]), .mul(mul_1_mul));
  Div #(.Bits(8)) div_1 (.a(A), .b(B), .q(div_1_q), .r(div_1_r));
  ROM #(.AddrBits(6), .Bits(8)) rom_1 (.A({A[2:0], B[2:0]}), .sel(as), .D(rom_1_d));
  assign and_10_out = A & B;  // And and_10, 8 bits wide
  assign or_9_out = A | B;  // Or or_9, 8 bits wide
  assign xor_1_out = A ^ B;  // XOr xor_1, 8 bits wide
  BarrelShifter #(.Bits(8)) barrelshifter_1 (.in(A), .shift(B[3:0]), .out(barrelshifter_1_out));
  Comparator #(.Bits(8)) comparator_5 (.a(A), .b(B), .gt(comparator_5_gt), .eq(comparator_5_eq), .lt(comparator_5_lt));
  and and_11 (and_11_out, sigJump_eq, eFlag);
  assign not_1_out = ~A;  // Not not_1, 8 bits wide
  ROM #(.AddrBits(8)) prime (.A(A), .sel(1'b1), .D(prime_d));
  and and_12 (and_12_out, gFlag, ~re);  // And
  Multiplexer #(.Selector_Bits(4), .Bits(8)) multiplexer_10 (
    .sel(d_ff_9_q), .in_0(operand), .in_1(B), .in_2(C), .in_3(Noperand), .in_4(rA), .in_5(add_2_s),
    .in_6(sub_1_s), .in_7(mul_1_mul), .in_8(div_1_q), .in_9(div_1_r), .in_10(rom_1_d), .in_11(not_1_out),
    .in_12(and_10_out), .in_13(or_9_out), .in_14(xor_1_out), .in_15(barrelshifter_1_out),
    .out(multiplexer_10_out));
  D_FF #(.Bits(4)) d_ff_9 (.D(a_store_d), .C(clk), .Q(d_ff_9_q));  // open: nQ
  Multiplexer multiplexer_11 (.sel(sigComp), .in_0(and_12_out), .in_1(comparator_5_gt), .out(gFlag));
  and and_13 (and_13_out, sigJump_gt, gFlag);
  Multiplexer #(.Bits(8)) multiplexer_12 (.sel(sigB), .in_0(A), .in_1(operand), .out(multiplexer_12_out));
  ROM #(.AddrBits(5), .Bits(4)) a_store (.A(opcode), .sel(1'b1), .D(a_store_d));
  ROM #(.AddrBits(5), .Bits(2)) c_store (.A(opcode), .sel(1'b1), .D(c_store_d));
  or or_10 (jump, and_11_out, and_13_out, and_14_out, and_15_out, and_18_out);
  and and_14 (and_14_out, sigJump, sigJump);
  Multiplexer #(.Bits(8)) multiplexer_13 (
    .sel(re), .in_0(multiplexer_10_out), .in_1({8{1'b0}}), .out(multiplexer_13_out));
  Multiplexer multiplexer_14 (.sel(sigPrime), .in_0(comparator_5_eq), .in_1(prime_d), .out(multiplexer_14_out));
  and and_15 (and_15_out, sigJump_lt, lFlag);
  Register #(.Bits(8)) accA (.D(multiplexer_13_out), .C(clk), .en(or_11_out), .Q(A));
  or or_11 (or_11_out, as, re);
  Multiplexer #(.Bits(8)) multiplexer_15 (
    .sel(re), .in_0(multiplexer_12_out), .in_1({8{1'b0}}), .out(multiplexer_15_out));
  D_FF #(.Bits(2)) d_ff_10 (.D(c_store_d), .C(clk), .Q(d_ff_10_q));  // open: nQ
  and and_16 (and_16_out, eFlag, ~re);  // And
  or or_12 (or_12_out, sigComp, sigPrime);
  or or_13 (or_13_out, bs, re);
  Multiplexer #(.Selector_Bits(2), .Bits(8)) multiplexer_16 (
    .sel(d_ff_10_q), .in_0({8{1'b0}}), .in_1(A), .in_2(M), .in_3(N), .out(multiplexer_16_out));
  and and_17 (and_17_out, lFlag, ~re);  // And
  ROM #(.AddrBits(5), .Bits(10)) rom_2 (.A(opcode), .sel(1'b1), .D(rom_2_d));
  and and_18 (and_18_out, sigJump_eq__gt, or_14_out);
  Register #(.Bits(8)) accB (.D(multiplexer_15_out), .C(clk), .en(or_13_out), .Q(B));
  Multiplexer multiplexer_17 (.sel(or_12_out), .in_0(and_16_out), .in_1(multiplexer_14_out), .out(eFlag));
  Multiplexer multiplexer_18 (.sel(sigComp), .in_0(and_17_out), .in_1(comparator_5_lt), .out(lFlag));
  D_FF #(.Bits(10)) d_ff_11 (
    .D(rom_2_d), .C(clk),
    .Q({readRam, sigPrime, sigComp, sigJump_eq__gt, sigJump_lt, sigJump_gt, sigJump_eq, sigJump, sigRam, sigB}));  // open: nQ
  or or_14 (or_14_out, eFlag, gFlag);
  ROM #(.AddrBits(5), .Bits(3)) abc_store (.A(opcode), .sel(1'b1), .D(abc_store_d));
  Multiplexer #(.Bits(8)) multiplexer_19 (
    .sel(re), .in_0(multiplexer_16_out), .in_1({8{1'b0}}), .out(multiplexer_19_out));
  D_FF #(.Bits(3)) d_ff_12 (.D(abc_store_d), .C(clk), .Q({as, bs, cs}));  // open: nQ
  Register #(.Bits(8)) regC (.D(multiplexer_19_out), .C(clk), .en(or_15_out), .Q(C));
  or or_15 (or_15_out, cs, re);

  // Other names for the same wires on the sheet: in[12:0] = progIN; load = progLoad; retemp = result

  // Notes on the sheet:
  //   rRAM
  //   start hold
  //   pRAM
  //   result hold
  //   valid
  //   reset hold
  //   Done
  //   opcode(store ABC)
  //   contents of rom_1 (hex, n*v repeats v):
  //   1,7*0,9*1,2,4,8,10,20,40,80,1,3,9,1b,51,f3,d9,8b,1,4,10,40,a00
  //   ,0,0,0,1,5,19,7d,71,35,9,2d,1,6,24,d8,10,60,40,80,1,7,31,57,61
  //   ,a7,91,f7
  //   opcode(comp&prime)
  //   opcode(Jump)
  //   contents of prime (hex, n*v repeats v):
  //   0,0,1,1,0,1,0,1,0,0,0,1,0,1,0,0,0,1,0,1,0,0,0,1,5*0,1,0,1,5*0
  //   ,1,0,0,0,1,0,1,0,0,0,1,5*0,1,5*0,1,0,1,5*0,1,0,0,0,1,0,1,5*0,1
  //   ,0,0,0,1,5*0,1,7*0,1,0,0,0,1,0,1,0,0,0,1,0,1,0,0,0,1,13*0,1,0,0,0
  //   ,1,5*0,1,0,1,9*0,1,0,1,5*0,1,5*0,1,0,0,0,1,5*0,1,5*0,1,0,1,9*0
  //   ,1,0,1,0,0,0,1,0,1,11*0,1,11*0,1,0,0,0,1,0,1,0,0,0,1,5*0,1,0,1
  //   ,9*0,1
  //   contents of a_store (hex, n*v repeats v):
  //   0,0,0,1,0,0,2,0,0,3,4,6*0,5,6,7,8,9,a,0,b,c,d,e,f
  //   contents of c_store (hex, n*v repeats v):
  //   5*0,1,0,2,3
  //   contents of rom_2 (hex, n*v repeats v):
  //   0,0,1,7*0,200,2,4,8,10,20,40,6*0,80,5*0,100
  //   contents of abc_store (hex, n*v repeats v):
  //   0,4,2,4,2,1,4,1,1,4,4,6*0,6*4,0,5*4
endmodule
